# Fritzing sketch RoboToy (saved by Fritzing 0.9.3b)
circuit board: 8.46667cm x 5.64444cm

parts:
  TSOP4838 = TSOP312.., 314.. [package=THT]
  TSOP4838_2 = TSOP312.., 314.. [package=THT]
  TSOP4838_3 = TSOP312.., 314.. [package=THT]
  TSOP4838_4 = TSOP312.., 314.. [package=THT]
  Raspberry_Pi_1 = Raspberry Pi 3 [part_number=RPI-3-V1.2]
  LED = LED - 3mm [color="Yellow (595nm)" package="3 mm [THT]"]
  TSAL6200 = LED - 3mm [color="Infrared (940nm)" package="3 mm [THT]"]
  R5 = Resistor [tolerance=±5% resistance=220 package=THT]
  R6 = Resistor [tolerance=±5% resistance=220 package=THT]
  BC547 = NPN-Transistor [package="TO92 [THT]"]
  R7 = Resistor [tolerance=±5% resistance=10k package=THT]
  RGB = RGB LED (com. anode, rbg) [package="5 mm [THT]"]
  R8 = Resistor [tolerance=±5% resistance=47 package=THT]
  R9 = Resistor [tolerance=±5% resistance=47 package=THT]
  R10 = Resistor [tolerance=±5% resistance=100 package=THT]

nets (from the breadboard view):
  GND: TSOP4838.GND, TSOP4838_2.GND, TSOP4838_3.GND, TSOP4838_4.GND, Raspberry_Pi_1.GND, BC547.E
  N1: TSOP4838.Vs, TSOP4838_2.Vs, TSOP4838_3.Vs, TSOP4838_4.Vs, Raspberry_Pi_1.5V, R5.Pin_0, R6.Pin_0
  N2: TSOP4838.Data, Raspberry_Pi_1.GPIO27
  N3: TSOP4838_2.Data, Raspberry_Pi_1.GPIO23
  N4: TSOP4838_3.Data, Raspberry_Pi_1.GPIO22
  N5: TSOP4838_4.Data, Raspberry_Pi_1.GPIO24
  3V3: Raspberry_Pi_1.3v3, Raspberry_Pi_1.3V3, RGB.common_anode
  N6: Raspberry_Pi_1.GPIO21, R8.Pin_1
  N7: Raspberry_Pi_1.GPIO20, R9.Pin_1
  N8: Raspberry_Pi_1.GPIO16, R10.Pin_1
  N9: Raspberry_Pi_1.GPIO18, R7.Pin_1
  N10: LED.cathode, TSAL6200.cathode, BC547.C
  N11: LED.anode, R6.Pin_1
  N12: TSAL6200.anode, R5.Pin_1
  N13: BC547.B, R7.Pin_0
  N14: RGB.red_cathode, R10.Pin_0
  N15: RGB.blue_cathode, R8.Pin_0
  N16: RGB.green_cathode, R9.Pin_0
